// Logisim project CS1409_U201414815_胡超_CPU.circ as structural Verilog: 7 circuits, main circuit main
module main (
);

  wire alu_2_equal, and_2_out, and_3_out, clk, clock_1_out, comparator_1_eq, controller_1_alusrc,
       controller_1_beq, controller_1_bne, controller_1_memread, controller_1_memtoreg,
       controller_1_memwrite, controller_1_regdst, controller_1_regwrite, controller_1_shift, halt, IX, J,
       Jr, JX, not_1_out, or_1_out, RX, Syscall;
  wire [3:0] controller_1_aluop, register_1_q, register_1_q_3, register_1_q_4, register_1_q_5, register_1_q_6;
  wire [4:0] ifu_1_rd, ifu_1_rs, ifu_1_rt, ifu_1_shamt, multiplexer_3_out, multiplexer_4_out;
  wire [5:0] ifu_1_funct, ifu_1_op;
  wire [9:0] b_Select_2_out_2, b_Select_out_2;
  wire [15:0] ifu_1_immediate16;
  wire [15:4] register_1_q_2;
  wire [25:0] ifu_1_immediate26;
  wire [31:0] a0, adder_1_out, adder_2_out, alu_2_result, alu_3_result, bit_extender_2_out,
       bit_extender_3_out, counter_1_out_3, counter_2_out_3, counter_3_out_3, counter_4_out_3, main_1_reg1,
       main_1_reg2_2, main_1_s0_value, multiplexer_1_out, multiplexer_5_out, multiplexer_6_out,
       multiplexer_7_out, multiplexer_8_out, multiplexer_9_out, multiplexer_10_out, multiplexer_11_out,
       multiplexer_12_out, multiplexer_13_out, pc_4, PC_q, ram_1_data, rom_1_data, shamt, shifter_1_out, v0;

  Register #(.width(32)) PC (.D(multiplexer_1_out), .Q(PC_q), .clk(clk));  // open: en, clr
  Multiplexer #(.width(32), .enable("false")) multiplexer_1 (
    .in0(pc_4), .in1(multiplexer_6_out), .out(multiplexer_1_out), .sel(or_1_out));
  Multiplexer #(.enable("false")) multiplexer_2 (.in0(clock_1_out), .in1(1'b0), .out(clk), .sel(halt));
  Clock clock_1 (.out(clock_1_out));
  b_Select b_Select (.in_1(PC_q), .out_2(b_Select_out_2));
  // Probe on pc_4
  // Probe on multiplexer_6_out
  ALU alu_1 (
    .AluOP(4'b0101), .X(PC_q), .Result(pc_4), .Y(32'h4));  // open: Equal, Signed_Overflow, UnSigned_Overflow, Result2
  IFU ifu_1 (
    .instructions(rom_1_data), .op(ifu_1_op), .funct(ifu_1_funct), .shamt(ifu_1_shamt), .Rd(ifu_1_rd),
    .immediate16(ifu_1_immediate16), .Rt(ifu_1_rt), .Rs(ifu_1_rs), .immediate26(ifu_1_immediate26));
  ROM #(.addrWidth(10), .dataWidth(32)) rom_1 (.addr(b_Select_out_2), .data(rom_1_data));  // open: sel
  // Probe on ifu_1_immediate26
  assign shamt = {{27{1'b0}}, ifu_1_shamt};  // Bit_Extender bit_extender_1
  Multiplexer #(.width(5), .enable("false")) multiplexer_3 (
    .in0(ifu_1_rt), .in1(ifu_1_rd), .out(multiplexer_3_out), .sel(controller_1_regdst));
  Comparator #(.width(32)) comparator_1 (.a(v0), .b(32'ha), .eq(comparator_1_eq));  // open: gt, lt
  Controller controller_1 (
    .op(ifu_1_op), .funct(ifu_1_funct), .RegWrite(controller_1_regwrite), .ALUSrc(controller_1_alusrc),
    .MemWrite(controller_1_memwrite), .MemRead(controller_1_memread), .MemtoReg(controller_1_memtoreg),
    .RegDst(controller_1_regdst), .ALUOp(controller_1_aluop), .J(J), .Beq(controller_1_beq),
    .Bne(controller_1_bne), .Jr(Jr), .Shift(controller_1_shift), .Syscall(Syscall), .RX(RX), .IX(IX), .JX(JX));
  Multiplexer #(.width(5), .enable("false")) multiplexer_4 (
    .in0(multiplexer_3_out), .in1({5{1'b1}}), .out(multiplexer_4_out), .sel(J));
  assign bit_extender_2_out = {{16{ifu_1_immediate16[15]}}, ifu_1_immediate16};  // Bit_Extender bit_extender_2
  assign bit_extender_3_out = {{6{ifu_1_immediate26[25]}}, ifu_1_immediate26};  // Bit_Extender bit_extender_3
  and and_1 (halt, Syscall, comparator_1_eq);
  or or_1 (or_1_out, and_2_out, and_3_out, Jr, J);
  Multiplexer #(.width(32), .enable("false")) multiplexer_5 (
    .in0(pc_4), .in1({32{1'b0}}), .out(multiplexer_5_out), .sel(J));
  Multiplexer #(.width(32), .enable("false")) multiplexer_6 (
    .in0(alu_3_result), .in1(main_1_reg1), .out(multiplexer_6_out), .sel(Jr));
  // Probe on main_1_s0_value
  \CS1409_U201414815_胡超_regfile_1_main  main_1 (
    .Reg1_num(ifu_1_rs), .Reg2(ifu_1_rt), .Write_Reg_num(multiplexer_4_out), .Din(multiplexer_9_out),
    .Write_Enable(controller_1_regwrite), .Clock(clk), .Reg1(main_1_reg1), .Reg2_2(main_1_reg2_2),
    .s0_Value(main_1_s0_value), .out_12(v0), .out_13(a0));  // open: s1_Value, s2_Value, ra_Value
  Multiplexer #(.width(32), .enable("false")) multiplexer_7 (
    .in0(bit_extender_2_out), .in1(bit_extender_3_out), .out(multiplexer_7_out), .sel(J));
  Hex_Digit_Display hex_digit_display_1 (.value(register_1_q_5));  // open: dp
  Hex_Digit_Display hex_digit_display_2 (.value(register_1_q_6));  // open: dp
  and and_2 (and_2_out, alu_2_equal, controller_1_beq);
  and and_3 (and_3_out, not_1_out, controller_1_bne);
  Multiplexer #(.width(32), .enable("false")) multiplexer_8 (
    .in0(main_1_reg2_2), .in1(bit_extender_2_out), .out(multiplexer_8_out), .sel(controller_1_alusrc));
  Multiplexer #(.width(32), .enable("false")) multiplexer_9 (
    .in0(multiplexer_13_out), .in1(pc_4), .out(multiplexer_9_out), .sel(J));
  // Probe on multiplexer_9_out
  Hex_Digit_Display hex_digit_display_3 (.value(register_1_q_4));  // open: dp
  not not_1 (not_1_out, alu_2_equal);
  Multiplexer #(.width(32), .enable("false")) multiplexer_10 (
    .in0(main_1_reg1), .in1(main_1_reg2_2), .out(multiplexer_10_out), .sel(controller_1_shift));
  Multiplexer #(.width(32), .enable("false")) multiplexer_11 (
    .in0(multiplexer_8_out), .in1(shamt), .out(multiplexer_11_out), .sel(controller_1_shift));
  Hex_Digit_Display hex_digit_display_4 (.value(register_1_q_3));  // open: dp
  Hex_Digit_Display hex_digit_display_5 (.value(register_1_q_2[15:12]));  // open: dp
  Register #(.width(32)) register_1 (
    .D(a0),
    .Q({register_1_q_6, register_1_q_5, register_1_q_4, register_1_q_3, register_1_q_2, register_1_q}),
    .clk(clk));  // open: en, clr
  ALU alu_2 (
    .AluOP(controller_1_aluop), .X(multiplexer_10_out), .Equal(alu_2_equal), .Result(alu_2_result),
    .Y(multiplexer_11_out));  // open: Signed_Overflow, UnSigned_Overflow, Result2
  // Probe on controller_1_aluop
  Shifter #(.width(32)) shifter_1 (.in(multiplexer_7_out), .\dist (5'b00010), .out(shifter_1_out));
  Hex_Digit_Display hex_digit_display_6 (.value(register_1_q_2[11:8]));  // open: dp
  ALU alu_3 (
    .AluOP(4'b0101), .X(shifter_1_out), .Result(alu_3_result), .Y(multiplexer_5_out));  // open: Equal, Signed_Overflow, UnSigned_Overflow, Result2
  Hex_Digit_Display hex_digit_display_7 (.value(register_1_q_2[7:4]));  // open: dp
  Hex_Digit_Display hex_digit_display_8 (.value(register_1_q));  // open: dp
  b_Select b_Select_2 (.in_1(alu_2_result), .out_2(b_Select_2_out_2));
  Multiplexer #(.width(32), .enable("false")) multiplexer_12 (
    .in0({32{1'b0}}), .in1(32'h1), .out(multiplexer_12_out), .sel(halt));
  counter counter_1 (.in_1(1'b1), .in_2(clk), .out_3(counter_1_out_3));
  RAM #(.addrWidth(10), .dataWidth(32), .bus("separate")) ram_1 (
    .addr(b_Select_2_out_2), .din(main_1_reg2_2), .data(ram_1_data), .str(controller_1_memwrite), .clk(clk),
    .ld(controller_1_memread));  // open: sel, clr
  // Probe on adder_1_out
  Adder #(.width(32)) adder_1 (.a(multiplexer_12_out), .b(counter_1_out_3), .out(adder_1_out));  // open: cin, cout
  Multiplexer #(.width(32), .enable("false")) multiplexer_13 (
    .in0(alu_2_result), .in1(ram_1_data), .out(multiplexer_13_out), .sel(controller_1_memtoreg));
  counter counter_2 (.in_1(RX), .in_2(clk), .out_3(counter_2_out_3));
  // Probe on adder_2_out
  Adder #(.width(32)) adder_2 (.a(multiplexer_12_out), .b(counter_2_out_3), .out(adder_2_out));  // open: cin, cout
  // Probe on counter_3_out_3
  counter counter_3 (.in_1(IX), .in_2(clk), .out_3(counter_3_out_3));
  // Probe on counter_4_out_3
  counter counter_4 (.in_1(JX), .in_2(clk), .out_3(counter_4_out_3));

  // Notes on the sheet:
  //   contents of rom_1 (hex, n*v repeats v):
  //   20110001 8000c05 20110001 20120002 20130003 8000c09 20110001 20120002 20130003 8000c0d 20110001
  //   20120002 20130003 8000c11 20110001 20120002 20130003 c000cb8 20100001 20110001 118fc0 112020
  //   20020022 c 118882 12200001 8000c15 112020 20020022 c 20110001 118880 112020 20020022 c 12200001
  //   8000c1f 20110001 118fc0 112020 20020022 c 1188c3 112020 20020022 c 118903 112020 20020022 c 118903
  //   112020 20020022 c 118903 112020 20020022 c 118903 112020 20020022 c 118903 112020 20020022 c 118903
  //   112020 20020022 c 118903 112020 20020022 c 20100001 109fc0 139fc3 8021 2012000c 24160003 26100001
  //   3210000f 20080008 20090001 139900 2709825 132020 20020022 c 1094022 1500fff9 22100001 2018000f
  //   2188024 108700 20080008 20090001 139902 2709825 132021 20020022 c 1094022 1500fff9 108702 2c9b022
  //   12c00001 8000c50 4020 1084027 84400 3508ffff 82021 20020022 c 2010ffff 20110000 ae300000 22100001
  //   22310004 ae300000 22100001 22310004 ae300000 22100001 22310004 ae300000 22100001 22310004 ae300000
  //   22100001 22310004 ae300000 22100001 22310004 ae300000 22100001 22310004 ae300000 22100001 22310004
  //   ae300000 22100001 22310004 ae300000 22100001 22310004 ae300000 22100001 22310004 ae300000 22100001
  //   22310004 ae300000 22100001 22310004 ae300000 22100001 22310004 ae300000 22100001 22310004 ae300000
  //   22100001 22310004 22100001 8020 2011003c 8e130000 8e340000 274402a 11000002 ae330000 ae140000
  //   2231fffc 1611fff8 102020 20020022 c 22100004 2011003c 1611fff2 2002000a c 20100000 22100001 102020
  //   20020022 c 22100002 102020 20020022 c 22100003 102020 20020022 c 22100004 102020 20020022 c 22100005
  //   102020 20020022 c 22100006 102020 20020022 c 22100007 102020 20020022 c 22100008 102020 20020022
  //   20020022 c 3e00008
endmodule

module SFIFU (
  input  op5,
  input  op4,
  input  op3,
  input  op2,
  input  op1,
  input  op0,
  input  funct5,
  input  funct4,
  input  funct3,
  input  funct2,
  input  funct1,
  input  funct0,
  output add,
  output addi,
  output addiu,
  output addu,
  output \and ,
  output andi,
  output sll,
  output sra,
  output srl,
  output sub,
  output \or ,
  output ori
);

  wire not_1_out, not_2_out, not_3_out, not_4_out, not_5_out, not_6_out, not_7_out, not_8_out, not_9_out,
       not_10_out, not_11_out, not_12_out, not_13_out, not_14_out, not_15_out, not_16_out, not_17_out,
       not_18_out, not_19_out, not_20_out, not_21_out, not_22_out, not_23_out, not_24_out, not_25_out,
       not_26_out, not_27_out, not_28_out, not_29_out, not_30_out, not_31_out, not_32_out, not_33_out,
       not_34_out, not_35_out, not_36_out, not_37_out, not_38_out, not_39_out, not_40_out, not_41_out,
       not_42_out, not_43_out, not_44_out, not_45_out, not_46_out, not_47_out, not_48_out, not_49_out,
       not_50_out, not_51_out, not_52_out, not_53_out, not_54_out, not_55_out, not_56_out, not_57_out,
       not_58_out, not_59_out, not_60_out, not_61_out, not_62_out, not_63_out, not_64_out, not_65_out,
       not_66_out, not_67_out, not_68_out, not_69_out, not_70_out, not_71_out, not_72_out, not_73_out,
       not_74_out, not_75_out, not_76_out, not_77_out, not_78_out, not_79_out, not_80_out, not_81_out,
       not_82_out, not_83_out, not_84_out, not_85_out, not_86_out, not_87_out, not_88_out, not_89_out,
       not_90_out, not_91_out, not_92_out, not_93_out, not_94_out, not_95_out, not_96_out, not_97_out,
       not_98_out, not_99_out;

  not not_1 (not_1_out, op5);
  not not_2 (not_2_out, op4);
  not not_3 (not_3_out, op3);
  not not_4 (not_4_out, op2);
  not not_5 (not_5_out, op1);
  not not_6 (not_6_out, op0);
  not not_7 (not_7_out, funct4);
  not not_8 (not_8_out, funct3);
  not not_9 (not_9_out, funct2);
  not not_10 (not_10_out, funct1);
  not not_11 (not_11_out, funct0);
  not not_12 (not_12_out, op5);
  not not_13 (not_13_out, op4);
  not not_14 (not_14_out, op2);
  not not_15 (not_15_out, op1);
  not not_16 (not_16_out, op0);
  not not_17 (not_17_out, op5);
  not not_18 (not_18_out, op4);
  not not_19 (not_19_out, op2);
  not not_20 (not_20_out, op1);
  not not_21 (not_21_out, op5);
  not not_22 (not_22_out, op4);
  not not_23 (not_23_out, op3);
  not not_24 (not_24_out, op2);
  not not_25 (not_25_out, op1);
  not not_26 (not_26_out, op0);
  not not_27 (not_27_out, funct4);
  not not_28 (not_28_out, funct3);
  not not_29 (not_29_out, funct2);
  not not_30 (not_30_out, funct1);
  not not_31 (not_31_out, op5);
  not not_32 (not_32_out, op4);
  not not_33 (not_33_out, op3);
  not not_34 (not_34_out, op2);
  not not_35 (not_35_out, op1);
  not not_36 (not_36_out, op0);
  not not_37 (not_37_out, funct4);
  not not_38 (not_38_out, funct3);
  not not_39 (not_39_out, funct1);
  not not_40 (not_40_out, funct0);
  not not_41 (not_41_out, op5);
  not not_42 (not_42_out, op4);
  not not_43 (not_43_out, op1);
  not not_44 (not_44_out, op0);
  not not_45 (not_45_out, op5);
  not not_46 (not_46_out, op4);
  not not_47 (not_47_out, op3);
  not not_48 (not_48_out, op2);
  not not_49 (not_49_out, op1);
  not not_50 (not_50_out, op0);
  not not_51 (not_51_out, funct5);
  not not_52 (not_52_out, funct4);
  not not_53 (not_53_out, funct3);
  not not_54 (not_54_out, funct2);
  not not_55 (not_55_out, funct1);
  not not_56 (not_56_out, funct0);
  not not_57 (not_57_out, op5);
  not not_58 (not_58_out, op4);
  not not_59 (not_59_out, op3);
  not not_60 (not_60_out, op2);
  not not_61 (not_61_out, op1);
  not not_62 (not_62_out, op0);
  not not_63 (not_63_out, funct5);
  not not_64 (not_64_out, funct4);
  not not_65 (not_65_out, funct3);
  not not_66 (not_66_out, funct2);
  not not_67 (not_67_out, op5);
  not not_68 (not_68_out, op4);
  not not_69 (not_69_out, op3);
  not not_70 (not_70_out, op2);
  not not_71 (not_71_out, op1);
  not not_72 (not_72_out, op0);
  not not_73 (not_73_out, funct5);
  not not_74 (not_74_out, funct4);
  not not_75 (not_75_out, funct3);
  not not_76 (not_76_out, funct2);
  not not_77 (not_77_out, funct0);
  not not_78 (not_78_out, op5);
  not not_79 (not_79_out, op4);
  not not_80 (not_80_out, op3);
  not not_81 (not_81_out, op2);
  not not_82 (not_82_out, op1);
  not not_83 (not_83_out, op0);
  not not_84 (not_84_out, funct4);
  not not_85 (not_85_out, funct3);
  not not_86 (not_86_out, funct2);
  not not_87 (not_87_out, funct0);
  not not_88 (not_88_out, op5);
  not not_89 (not_89_out, op4);
  not not_90 (not_90_out, op3);
  not not_91 (not_91_out, op2);
  not not_92 (not_92_out, op1);
  not not_93 (not_93_out, op0);
  not not_94 (not_94_out, funct4);
  not not_95 (not_95_out, funct3);
  not not_96 (not_96_out, funct1);
  not not_97 (not_97_out, op5);
  not not_98 (not_98_out, op4);
  not not_99 (not_99_out, op1);
  and and_1 (add, not_1_out, not_2_out, not_3_out, not_4_out, not_5_out, not_6_out, funct5, not_7_out, not_8_out, not_9_out, not_10_out, not_11_out);
  and and_2 (addi, not_12_out, not_13_out, op3, not_14_out, not_15_out, not_16_out);
  and and_3 (addiu, not_17_out, not_18_out, op3, not_19_out, not_20_out, op0);
  and and_4 (addu, not_21_out, not_22_out, not_23_out, not_24_out, not_25_out, not_26_out, funct5, not_27_out, not_28_out, not_29_out, not_30_out, funct0);
  and and_5 (\and , not_31_out, not_32_out, not_33_out, not_34_out, not_35_out, not_36_out, funct5, not_37_out, not_38_out, funct2, not_39_out, not_40_out);
  and and_6 (andi, not_41_out, not_42_out, op3, op2, not_43_out, not_44_out);
  and and_7 (sll, not_45_out, not_46_out, not_47_out, not_48_out, not_49_out, not_50_out, not_51_out, not_52_out, not_53_out, not_54_out, not_55_out, not_56_out);
  and and_8 (sra, not_57_out, not_58_out, not_59_out, not_60_out, not_61_out, not_62_out, not_63_out, not_64_out, not_65_out, not_66_out, funct1, funct0);
  and and_9 (srl, not_67_out, not_68_out, not_69_out, not_70_out, not_71_out, not_72_out, not_73_out, not_74_out, not_75_out, not_76_out, funct1, not_77_out);
  and and_10 (sub, not_78_out, not_79_out, not_80_out, not_81_out, not_82_out, not_83_out, funct5, not_84_out, not_85_out, not_86_out, funct1, not_87_out);
  and and_11 (\or , not_88_out, not_89_out, not_90_out, not_91_out, not_92_out, not_93_out, funct5, not_94_out, not_95_out, funct2, not_96_out, funct0);
  and and_12 (ori, not_97_out, not_98_out, op3, op2, not_99_out, op0);
endmodule

module STIFU (
  input  op5,
  input  op4,
  input  op3,
  input  op2,
  input  op1,
  input  op0,
  input  funct5,
  input  funct4,
  input  funct3,
  input  funct2,
  input  funct1,
  input  funct0,
  output \nor ,
  output lw,
  output sw,
  output beq,
  output bne,
  output slt,
  output slti,
  output sltu,
  output j,
  output jal,
  output jr,
  output syscall
);

  wire not_1_out, not_2_out, not_3_out, not_4_out, not_5_out, not_6_out, not_7_out, not_8_out, not_9_out,
       not_10_out, not_11_out, not_12_out, not_13_out, not_14_out, not_15_out, not_16_out, not_17_out,
       not_18_out, not_19_out, not_20_out, not_21_out, not_22_out, not_23_out, not_24_out, not_25_out,
       not_26_out, not_27_out, not_28_out, not_29_out, not_30_out, not_31_out, not_32_out, not_33_out,
       not_34_out, not_35_out, not_36_out, not_37_out, not_38_out, not_39_out, not_40_out, not_41_out,
       not_42_out, not_43_out, not_44_out, not_45_out, not_46_out, not_47_out, not_48_out, not_49_out,
       not_50_out, not_51_out, not_52_out, not_53_out, not_54_out, not_55_out, not_56_out, not_57_out,
       not_58_out, not_59_out, not_60_out, not_61_out, not_62_out, not_63_out, not_64_out, not_65_out,
       not_66_out, not_67_out, not_68_out, not_69_out, not_70_out, not_71_out, not_72_out, not_73_out;

  not not_1 (not_1_out, op5);
  not not_2 (not_2_out, op4);
  not not_3 (not_3_out, op3);
  not not_4 (not_4_out, op2);
  not not_5 (not_5_out, op1);
  not not_6 (not_6_out, op0);
  not not_7 (not_7_out, funct4);
  not not_8 (not_8_out, funct3);
  not not_9 (not_9_out, op4);
  not not_10 (not_10_out, op3);
  not not_11 (not_11_out, op2);
  not not_12 (not_12_out, op4);
  not not_13 (not_13_out, op2);
  not not_14 (not_14_out, op5);
  not not_15 (not_15_out, op4);
  not not_16 (not_16_out, op3);
  not not_17 (not_17_out, op1);
  not not_18 (not_18_out, op0);
  not not_19 (not_19_out, op5);
  not not_20 (not_20_out, op4);
  not not_21 (not_21_out, op3);
  not not_22 (not_22_out, op1);
  not not_23 (not_23_out, op5);
  not not_24 (not_24_out, op4);
  not not_25 (not_25_out, op3);
  not not_26 (not_26_out, op2);
  not not_27 (not_27_out, op1);
  not not_28 (not_28_out, op0);
  not not_29 (not_29_out, funct4);
  not not_30 (not_30_out, funct2);
  not not_31 (not_31_out, funct0);
  not not_32 (not_32_out, op5);
  not not_33 (not_33_out, op4);
  not not_34 (not_34_out, op2);
  not not_35 (not_35_out, op0);
  not not_36 (not_36_out, op5);
  not not_37 (not_37_out, op4);
  not not_38 (not_38_out, op3);
  not not_39 (not_39_out, op2);
  not not_40 (not_40_out, op1);
  not not_41 (not_41_out, op0);
  not not_42 (not_42_out, funct4);
  not not_43 (not_43_out, funct2);
  not not_44 (not_44_out, op5);
  not not_45 (not_45_out, op4);
  not not_46 (not_46_out, op3);
  not not_47 (not_47_out, op2);
  not not_48 (not_48_out, op0);
  not not_49 (not_49_out, op5);
  not not_50 (not_50_out, op4);
  not not_51 (not_51_out, op3);
  not not_52 (not_52_out, op2);
  not not_53 (not_53_out, op5);
  not not_54 (not_54_out, op4);
  not not_55 (not_55_out, op3);
  not not_56 (not_56_out, op2);
  not not_57 (not_57_out, op1);
  not not_58 (not_58_out, op0);
  not not_59 (not_59_out, funct5);
  not not_60 (not_60_out, funct4);
  not not_61 (not_61_out, funct2);
  not not_62 (not_62_out, funct1);
  not not_63 (not_63_out, funct0);
  not not_64 (not_64_out, op5);
  not not_65 (not_65_out, op4);
  not not_66 (not_66_out, op3);
  not not_67 (not_67_out, op2);
  not not_68 (not_68_out, op1);
  not not_69 (not_69_out, op0);
  not not_70 (not_70_out, funct5);
  not not_71 (not_71_out, funct4);
  not not_72 (not_72_out, funct1);
  not not_73 (not_73_out, funct0);
  and and_1 (\nor , not_1_out, not_2_out, not_3_out, not_4_out, not_5_out, not_6_out, funct5, not_7_out, not_8_out, funct2, funct1, funct0);
  and and_2 (lw, op5, not_9_out, not_10_out, not_11_out, op1, op0);
  and and_3 (sw, op5, not_12_out, op3, not_13_out, op1, op0);
  and and_4 (beq, not_14_out, not_15_out, not_16_out, op2, not_17_out, not_18_out);
  and and_5 (bne, not_19_out, not_20_out, not_21_out, op2, not_22_out, op0);
  and and_6 (slt, not_23_out, not_24_out, not_25_out, not_26_out, not_27_out, not_28_out, funct5, not_29_out, funct3, not_30_out, funct1, not_31_out);
  and and_7 (slti, not_32_out, not_33_out, op3, not_34_out, op1, not_35_out);
  and and_8 (sltu, not_36_out, not_37_out, not_38_out, not_39_out, not_40_out, not_41_out, funct5, not_42_out, funct3, not_43_out, funct1, funct0);
  and and_9 (j, not_44_out, not_45_out, not_46_out, not_47_out, op1, not_48_out);
  and and_10 (jal, not_49_out, not_50_out, not_51_out, not_52_out, op1, op0);
  and and_11 (jr, not_53_out, not_54_out, not_55_out, not_56_out, not_57_out, not_58_out, not_59_out, not_60_out, funct3, not_61_out, not_62_out, not_63_out);
  and and_12 (syscall, not_64_out, not_65_out, not_66_out, not_67_out, not_68_out, not_69_out, not_70_out, not_71_out, funct3, funct2, not_72_out, not_73_out);
endmodule

module Controller (
  input  [5:0] op,
  input  [5:0] funct,
  output RX,
  output IX,
  output JX,
  output RegWrite,
  output ALUSrc,
  output MemWrite,
  output MemRead,
  output MemtoReg,
  output Beq,
  output Bne,
  output J,
  output Jr,
  output RegDst,
  output Shift,
  output Syscall,
  output [3:0] ALUOp
);

  wire sfifu_1_add, sfifu_1_addi, sfifu_1_addiu, sfifu_1_addu, sfifu_1_and, sfifu_1_andi, sfifu_1_or,
       sfifu_1_ori, sfifu_1_sll, sfifu_1_sra, sfifu_1_srl, sfifu_1_sub, stifu_1_j, stifu_1_jal, stifu_1_nor,
       stifu_1_slt, stifu_1_slti, stifu_1_sltu;

  SFIFU sfifu_1 (
    .op5(op[5]), .op4(op[4]), .op3(op[3]), .op2(op[2]), .op1(op[1]), .op0(op[0]), .funct5(funct[5]),
    .funct4(funct[4]), .funct3(funct[3]), .funct2(funct[2]), .funct1(funct[1]), .funct0(funct[0]),
    .add(sfifu_1_add), .addi(sfifu_1_addi), .addiu(sfifu_1_addiu), .addu(sfifu_1_addu), .\and (sfifu_1_and),
    .andi(sfifu_1_andi), .sll(sfifu_1_sll), .sra(sfifu_1_sra), .srl(sfifu_1_srl), .sub(sfifu_1_sub),
    .\or (sfifu_1_or), .ori(sfifu_1_ori));
  STIFU stifu_1 (
    .op5(op[5]), .op4(op[4]), .op3(op[3]), .op2(op[2]), .op1(op[1]), .op0(op[0]), .funct5(funct[5]),
    .funct4(funct[4]), .funct3(funct[3]), .funct2(funct[2]), .funct1(funct[1]), .funct0(funct[0]),
    .\nor (stifu_1_nor), .lw(MemRead), .sw(MemWrite), .beq(Beq), .bne(Bne), .slt(stifu_1_slt),
    .slti(stifu_1_slti), .sltu(stifu_1_sltu), .j(stifu_1_j), .jal(stifu_1_jal), .jr(Jr), .syscall(Syscall));
  or or_1 (RegWrite, sfifu_1_add, sfifu_1_addi, sfifu_1_addiu, sfifu_1_addu, sfifu_1_and, sfifu_1_andi, sfifu_1_sll, sfifu_1_sra, sfifu_1_srl, sfifu_1_sub, sfifu_1_or, sfifu_1_ori, stifu_1_nor, MemRead, stifu_1_slt, stifu_1_slti, stifu_1_sltu, stifu_1_jal);
  or ALUOp3 (ALUOp[3], sfifu_1_or, sfifu_1_ori, stifu_1_nor, stifu_1_slt, stifu_1_slti, stifu_1_sltu);
  or ALUOp2 (ALUOp[2], sfifu_1_add, sfifu_1_addi, sfifu_1_addiu, sfifu_1_addu, sfifu_1_and, sfifu_1_andi, sfifu_1_sub, MemRead, MemWrite, stifu_1_sltu, stifu_1_j, stifu_1_jal, Jr);
  or ALUOp1 (ALUOp[1], sfifu_1_and, sfifu_1_andi, sfifu_1_srl, sfifu_1_sub, stifu_1_nor, stifu_1_slt, stifu_1_slti);
  or ALUOp0 (ALUOp[0], sfifu_1_add, sfifu_1_addi, sfifu_1_addiu, sfifu_1_addu, sfifu_1_and, sfifu_1_andi, sfifu_1_sra, MemRead, MemWrite, stifu_1_slt, stifu_1_slti, stifu_1_j, stifu_1_jal, Jr);
  or or_2 (ALUSrc, sfifu_1_addi, sfifu_1_addiu, sfifu_1_andi, sfifu_1_ori, MemRead, MemWrite, stifu_1_slti);
  or or_3 (J, stifu_1_j, stifu_1_jal);
  or or_4 (RegDst, sfifu_1_add, sfifu_1_addu, sfifu_1_and, sfifu_1_sll, sfifu_1_sra, sfifu_1_srl, sfifu_1_sub, sfifu_1_or, stifu_1_nor, stifu_1_slt, stifu_1_sltu);
  or or_5 (Shift, sfifu_1_sll, sfifu_1_sra, sfifu_1_srl);
  or or_6 (RX, sfifu_1_add, sfifu_1_addu, sfifu_1_and, sfifu_1_sll, sfifu_1_sra, sfifu_1_srl, sfifu_1_sub, sfifu_1_or, stifu_1_nor, stifu_1_slt, stifu_1_sltu, Jr, Syscall);
  or or_7 (IX, sfifu_1_addi, sfifu_1_addiu, sfifu_1_andi, sfifu_1_ori, MemRead, MemWrite, Beq, Bne, stifu_1_slti);
  or or_8 (JX, stifu_1_j, stifu_1_jal);

  assign MemtoReg = MemRead;
endmodule

module IFU (
  input  [31:0] instructions,
  output [5:0] op,
  output [4:0] Rs,
  output [4:0] Rt,
  output [4:0] Rd,
  output [4:0] shamt,
  output [5:0] funct,
  output [15:0] immediate16,
  output [25:0] immediate26
);


  assign funct = instructions[5:0];
  assign immediate16 = instructions[15:0];
  assign immediate26 = instructions[25:0];
  assign op = instructions[31:26];
  assign Rd = instructions[15:11];
  assign Rs = instructions[25:21];
  assign Rt = instructions[20:16];
  assign shamt = instructions[10:6];
endmodule

module b_Select (
  input  [31:0] in_1,
  output [9:0] out_2
);


  assign out_2 = in_1[11:2];
endmodule

module counter (
  input  in_1,
  input  in_2,
  output [31:0] out_3
);

  wire [31:0] adder_1_out;

  Register #(.width(32)) register_1 (.D(adder_1_out), .en(in_1), .Q(out_3), .clk(in_2));  // open: clr
  Adder #(.width(32)) adder_1 (.a(32'h1), .b(out_3), .out(adder_1_out));  // open: cin, cout
endmodule
