// Logisim project CS1409_U201414815_胡超_alu.circ as structural Verilog: 6 circuits, main circuit ALU
module ALU (
  input  [31:0] X,
  input  [31:0] Y,
  input  [3:0] AluOP,
  output Signed_Overflow,
  output UnSigned_Overflow,
  output Equal,
  output [31:0] Result,
  output [31:0] Result2
);

  wire comparator_1_lt, comparator_2_lt, n32_bits_add_1_cout, n32_bits_add_1_v, n32_bits_add_2_cout,
       n32_bits_add_2_v, not_2_out;
  wire [4:0] bitselector_1_out;
  wire [31:0] and_1_out, bit_extender_1_out, bit_extender_2_out, divider_1_out, divider_1_rem,
       multiplier_1_cout, multiplier_1_out, n32_bits_add_1_out, n32_bits_add_2_out, not_1_out, not_3_out,
       or_1_out, shifter_1_out, shifter_2_out, shifter_3_out, xor_1_out;

  // Probe on X
  // Probe on X
  // Probe on Y
  // Probe on Y
  BitSelector #(.width(32), .group(5)) bitselector_1 (.in(Y), .out(bitselector_1_out), .sel(3'b000));
  // Probe on AluOP
  Shifter #(.width(32)) shifter_1 (.in(X), .\dist (bitselector_1_out), .out(shifter_1_out));
  Shifter #(.width(32), .shift("ar")) shifter_2 (.in(X), .\dist (bitselector_1_out), .out(shifter_2_out));
  Shifter #(.width(32), .shift("lr")) shifter_3 (.in(X), .\dist (bitselector_1_out), .out(shifter_3_out));
  Multiplier #(.width(32)) multiplier_1 (
    .a(X), .b(Y), .out(multiplier_1_out), .cin({32{1'b0}}), .cout(multiplier_1_cout));
  Divider #(.width(32)) divider_1 (.a(X), .b(Y), .out(divider_1_out), .upper({32{1'b0}}), .rem(divider_1_rem));
  _32_bits_add u_32_bits_add_1 (
    .Cout(n32_bits_add_1_cout), .out(n32_bits_add_1_out), .X(X), .Y(Y), .C0(1'b0), .V(n32_bits_add_1_v));
  _32_bits_add u_32_bits_add_2 (
    .Cout(n32_bits_add_2_cout), .out(n32_bits_add_2_out), .X(X), .Y(not_1_out), .C0(1'b1),
    .V(n32_bits_add_2_v));
  assign not_1_out = ~Y;  // NOT_Gate not_1, 32 bits wide
  assign and_1_out = X & Y;  // AND_Gate and_1, 32 bits wide
  assign or_1_out = X | Y;  // OR_Gate or_1, 32 bits wide
  assign xor_1_out = X ^ Y;  // XOR_Gate xor_1, 32 bits wide
  Comparator #(.width(32)) comparator_1 (.a(X), .b(Y), .eq(Equal), .lt(comparator_1_lt));  // open: gt
  Comparator #(.width(32), .mode("unsigned")) comparator_2 (.a(X), .b(Y), .lt(comparator_2_lt));  // open: gt, eq
  // Probe on Result
  // Probe on Result
  not not_2 (not_2_out, n32_bits_add_2_cout);
  assign not_3_out = ~or_1_out;  // NOT_Gate not_3, 32 bits wide
  assign bit_extender_1_out = {{31{1'b0}}, comparator_1_lt};  // Bit_Extender bit_extender_1
  assign bit_extender_2_out = {{31{1'b0}}, comparator_2_lt};  // Bit_Extender bit_extender_2
  // Probe on Result2
  Multiplexer #(.select(4), .width(32), .enable("false")) multiplexer_1 (
    .in0(shifter_1_out), .in1(shifter_2_out), .in2(shifter_3_out), .in3(multiplier_1_out),
    .in4(divider_1_out), .in5(n32_bits_add_1_out), .in6(n32_bits_add_2_out), .in7(and_1_out), .in8(or_1_out),
    .in9(xor_1_out), .in10(not_3_out), .in11(bit_extender_1_out), .in12(bit_extender_2_out),
    .in13({32{1'b0}}), .in14({32{1'b0}}), .in15({32{1'b0}}), .out(Result), .sel(AluOP));
  Multiplexer #(.select(4), .width(32), .enable("false")) multiplexer_2 (
    .in0({32{1'b0}}), .in1({32{1'b0}}), .in2({32{1'b0}}), .in3(multiplier_1_cout), .in4(divider_1_rem),
    .in5({32{1'b0}}), .in6({32{1'b0}}), .in7({32{1'b0}}), .in8({32{1'b0}}), .in9({32{1'b0}}),
    .in10({32{1'b0}}), .in11({32{1'b0}}), .in12({32{1'b0}}), .in13({32{1'b0}}), .in14({32{1'b0}}),
    .in15({32{1'b0}}), .out(Result2), .sel(AluOP));
  Multiplexer #(.select(4), .enable("false")) multiplexer_3 (
    .in0(1'b0), .in1(1'b0), .in2(1'b0), .in3(1'b0), .in4(1'b0), .in5(n32_bits_add_1_v),
    .in6(n32_bits_add_2_v), .in7(1'b0), .in8(1'b0), .in9(1'b0), .in10(1'b0), .in11(1'b0), .in12(1'b0),
    .in13(1'b0), .in14(1'b0), .in15(1'b0), .out(Signed_Overflow), .sel(AluOP));
  Multiplexer #(.select(4), .enable("false")) multiplexer_4 (
    .in0(1'b0), .in1(1'b0), .in2(1'b0), .in3(1'b0), .in4(1'b0), .in5(n32_bits_add_1_cout), .in6(not_2_out),
    .in7(1'b0), .in8(1'b0), .in9(1'b0), .in10(1'b0), .in11(1'b0), .in12(1'b0), .in13(1'b0), .in14(1'b0),
    .in15(1'b0), .out(UnSigned_Overflow), .sel(AluOP));

  // Other names for the same wires on the sheet: OF = Signed_Overflow; S[3:0] = AluOP; UOF = UnSigned_Overflow

  // Notes on the sheet:
  //   不要改变此引脚区域内容，也不要改变ALU封装形式
  //   输入引脚
  //   请在下方利用上方输入输出引脚的隧道信号构建ALU电路，ctrl+d复制选择部件
  //   华中科技大学计算机学院 计算机组成原理，鸣谢加州大学伯克利CS61C课程
  //   输出引脚
  //   探测区域
endmodule

module \演示电路  (
  input  [31:0] X,
  input  [31:0] Y,
  input  [3:0] ALUOP,
  output Signed_Overflow,
  output Unsigned_overflow,
  output [31:0] Result,
  output [31:0] Result_2,
  output Equal
);

  // Probe on X
  // Probe on X
  ALU alu_1 (
    .AluOP(ALUOP), .X(X), .Equal(Equal), .Result(Result), .Signed_Overflow(Signed_Overflow), .Y(Y),
    .UnSigned_Overflow(Unsigned_overflow), .Result2(Result_2));
  // Probe on ALUOP
  // Probe on Y
  // Probe on Y
  // Probe on Result
  // Probe on Result
  // Probe on Result_2

  // Notes on the sheet:
  //   ALu电路无需调整位置即可连接在该电路中，并且不能出现蓝色线缆和三态输出
endmodule

module \等差数列  (
  input  [31:0] \数列初始值 ,
  input  [31:0] \等差值 ,
  input  \时钟 ,
  output [31:0] Result
);

  // Probe on \数列初始值 
  // Probe on \数列初始值 
  // Probe on \等差值 
  // Probe on \等差值 
  // Probe on Result
  // Probe on Result

  // Other names for the same wires on the sheet: 数列初值[31:0] = \数列初始值 ; 累加和[31:0] = Result

  // Notes on the sheet:
  //   不要改变此引脚区域内容，也不要改变ALU封装形式
  //   请在下方利用上方输入输出引脚的隧道信号构建等差数列求和电路，ctrl+d复制选择部件
  //   华中科技大学计算机学院 计算机组成原理，鸣谢加州大学伯克利CS61C课程
  //   输出引脚
  //   探测区域
endmodule

module CLA (
  input  [3:0] G,
  input  [3:0] P,
  input  C0,
  output G_star,
  output P_star,
  output [3:0] Cout
);

  wire and_1_out, and_2_out, and_3_out, and_5_out, and_6_out, and_7_out, and_8_out, and_9_out, and_10_out,
       and_11_out, and_12_out, and_13_out, and_14_out;

  and and_1 (and_1_out, G[2], P[3]);
  ExactlyOne xor_1 (.out(G_star), .in0(G[3]), .in1(and_1_out), .in2(and_2_out), .in3(and_3_out));
  and and_2 (and_2_out, G[1], P[3], P[2]);
  and and_3 (and_3_out, G[0], P[3], P[2], P[1]);
  and and_4 (P_star, P[3], P[2], P[1], P[0]);
  and and_5 (and_5_out, G[2], P[3]);
  xor C4 (Cout[3], G[3], and_5_out, and_6_out, and_7_out, and_8_out);
  and and_6 (and_6_out, G[1], P[3], P[2]);
  and and_7 (and_7_out, G[0], P[3], P[2], P[1]);
  and and_8 (and_8_out, P[3], P[2], P[1], P[0], C0);
  xor C3 (Cout[2], G[2], and_9_out, and_10_out, and_11_out);
  and and_9 (and_9_out, G[1], P[2]);
  and and_10 (and_10_out, G[0], P[2], P[1]);
  and and_11 (and_11_out, P[2], P[1], P[0], C0);
  xor C2 (Cout[1], G[1], and_12_out, and_13_out);
  and and_12 (and_12_out, G[0], P[1]);
  and and_13 (and_13_out, P[1], P[0], C0);
  xor C1 (Cout[0], G[0], and_14_out);
  and and_14 (and_14_out, P[0], C0);
endmodule

module _4_bits_add (
  input  [3:0] X,
  input  [3:0] Y,
  input  C0,
  output [3:0] out,
  output Cout,
  output V,
  output G_star,
  output P_star
);

  wire [2:0] CLA_cout;
  wire [3:0] and_1_out, xor_4_out;

  xor xor_1 (V, Cout, CLA_cout[2]);
  xor xor_2 (out[3], CLA_cout[2], X[3], Y[3]);
  CLA CLA (.G(and_1_out), .P(xor_4_out), .C0(C0), .Cout({Cout, CLA_cout}), .P_star(P_star), .G_star(G_star));
  xor xor_3 (out[2], CLA_cout[1], X[2], Y[2]);
  assign and_1_out = X & Y;  // AND_Gate and_1, 4 bits wide
  assign xor_4_out = X ^ Y;  // XOR_Gate xor_4, 4 bits wide
  xor xor_5 (out[1], CLA_cout[0], X[1], Y[1]);
  xor xor_6 (out[0], X[0], Y[0], C0);
endmodule

module _32_bits_add (
  input  C0,
  input  [31:0] X,
  input  [31:0] Y,
  output V,
  output Cout,
  output [31:0] out
);

  wire [1:0] CLA_3_g_star, CLA_3_p_star;
  wire [3:0] CLA_2_cout, CLA_3_cout, CLA_cout, n4_bits_add_4_g_star, n4_bits_add_4_p_star,
       n4_bits_add_8_g_star, n4_bits_add_8_p_star;

  _4_bits_add u_4_bits_add_1 (
    .Cout(Cout), .X(X[31:28]), .Y(Y[31:28]), .out(out[31:28]), .C0(CLA_cout[2]),
    .P_star(n4_bits_add_4_p_star[3]), .G_star(n4_bits_add_4_g_star[3]), .V(V));
  _4_bits_add u_4_bits_add_2 (
    .X(X[27:24]), .Y(Y[27:24]), .out(out[27:24]), .C0(CLA_cout[1]), .P_star(n4_bits_add_4_p_star[2]),
    .G_star(n4_bits_add_4_g_star[2]));  // open: Cout, V
  _4_bits_add u_4_bits_add_3 (
    .X(X[23:20]), .Y(Y[23:20]), .out(out[23:20]), .C0(CLA_cout[0]), .P_star(n4_bits_add_4_p_star[1]),
    .G_star(n4_bits_add_4_g_star[1]));  // open: Cout, V
  CLA CLA (
    .G(n4_bits_add_4_g_star), .P(n4_bits_add_4_p_star), .C0(CLA_2_cout[0]), .Cout(CLA_cout),
    .P_star(CLA_3_p_star[1]), .G_star(CLA_3_g_star[1]));
  _4_bits_add u_4_bits_add_4 (
    .X(X[19:16]), .Y(Y[19:16]), .out(out[19:16]), .C0(CLA_2_cout[0]), .P_star(n4_bits_add_4_p_star[0]),
    .G_star(n4_bits_add_4_g_star[0]));  // open: Cout, V
  CLA CLA_2 (.G({2'b00, CLA_3_g_star}), .P({2'b00, CLA_3_p_star}), .C0(C0), .Cout(CLA_2_cout));  // open: P_star, G_star
  _4_bits_add u_4_bits_add_5 (
    .X(X[15:12]), .Y(Y[15:12]), .out(out[15:12]), .C0(CLA_3_cout[2]), .P_star(n4_bits_add_8_p_star[3]),
    .G_star(n4_bits_add_8_g_star[3]));  // open: Cout, V
  _4_bits_add u_4_bits_add_6 (
    .X(X[11:8]), .Y(Y[11:8]), .out(out[11:8]), .C0(CLA_3_cout[1]), .P_star(n4_bits_add_8_p_star[2]),
    .G_star(n4_bits_add_8_g_star[2]));  // open: Cout, V
  _4_bits_add u_4_bits_add_7 (
    .X(X[7:4]), .Y(Y[7:4]), .out(out[7:4]), .C0(CLA_3_cout[0]), .P_star(n4_bits_add_8_p_star[1]),
    .G_star(n4_bits_add_8_g_star[1]));  // open: Cout, V
  CLA CLA_3 (
    .G(n4_bits_add_8_g_star), .P(n4_bits_add_8_p_star), .C0(C0), .Cout(CLA_3_cout), .P_star(CLA_3_p_star[0]),
    .G_star(CLA_3_g_star[0]));
  _4_bits_add u_4_bits_add_8 (
    .X(X[3:0]), .Y(Y[3:0]), .out(out[3:0]), .C0(C0), .P_star(n4_bits_add_8_p_star[0]),
    .G_star(n4_bits_add_8_g_star[0]));  // open: Cout, V
endmodule
