// Logisim project alu.circ as structural Verilog: 6 circuits, main circuit ALU
module ALU (
  input  [31:0] X,
  input  [31:0] Y,
  input  [3:0] AluOP,
  output Signed_Overflow,
  output UnSigned_Overflow,
  output Equal,
  output [31:0] Result,
  output [31:0] Result_2
);

  wire [31:0] Result2;

  // Probe on X
  // Probe on X
  // Probe on Y
  // Probe on Y
  // Probe on AluOP
  // Probe on Result
  // Probe on Result
  // Probe on Result2

  // Other names for the same wires on the sheet: OF = Signed_Overflow; S[3:0] = AluOP; UOF = UnSigned_Overflow

  // Notes on the sheet:
  //   不要改变此引脚区域内容，也不要改变ALU封装形式
  //   输入引脚
  //   请在下方利用上方输入输出引脚的隧道信号构建ALU电路，ctrl+d复制选择部件
  //   华中科技大学计算机学院 计算机组成原理，鸣谢加州大学伯克利CS61C课程
  //   输出引脚
  //   探测区域
endmodule

module \演示电路  (
  input  [31:0] X,
  input  [31:0] Y,
  input  [3:0] ALUOP,
  output Signed_Overflow,
  output Unsigned_overflow,
  output [31:0] Result,
  output [31:0] Result_2,
  output Equal
);

  // Probe on X
  // Probe on X
  ALU alu_1 (
    .AluOP(ALUOP), .X(X), .Equal(Equal), .Result(Result), .Signed_Overflow(Signed_Overflow), .Y(Y),
    .Result_2(Result_2), .UnSigned_Overflow(Unsigned_overflow));
  // Probe on ALUOP
  // Probe on Y
  // Probe on Y
  // Probe on Result
  // Probe on Result
  // Probe on Result_2

  // Notes on the sheet:
  //   ALu电路无需调整位置即可连接在该电路中，并且不能出现蓝色线缆和三态输出
endmodule

module \等差数列  (
  input  [31:0] \数列初始值 ,
  input  [31:0] \等差值 ,
  input  \时钟 ,
  output [31:0] Result
);

  // Probe on \数列初始值 
  // Probe on \数列初始值 
  // Probe on \等差值 
  // Probe on \等差值 
  // Probe on Result
  // Probe on Result

  // Other names for the same wires on the sheet: 数列初值[31:0] = \数列初始值 ; 累加和[31:0] = Result

  // Notes on the sheet:
  //   不要改变此引脚区域内容，也不要改变ALU封装形式
  //   请在下方利用上方输入输出引脚的隧道信号构建等差数列求和电路，ctrl+d复制选择部件
  //   华中科技大学计算机学院 计算机组成原理，鸣谢加州大学伯克利CS61C课程
  //   输出引脚
  //   探测区域
endmodule

module CLA (
  input  [3:0] G,
  input  [3:0] P,
  input  C0,
  output G_star,
  output P_star,
  output [3:0] Cout
);

  wire and_1_out, and_2_out, and_3_out, and_5_out, and_6_out, and_7_out, and_8_out, and_9_out, and_10_out,
       and_11_out, and_12_out, and_13_out, and_14_out;

  and and_1 (and_1_out, G[2], P[3]);
  ExactlyOne xor_1 (.out(G_star), .in0(G[3]), .in1(and_1_out), .in2(and_2_out), .in3(and_3_out));
  and and_2 (and_2_out, G[1], P[3], P[2]);
  and and_3 (and_3_out, G[0], P[3], P[2], P[1]);
  and and_4 (P_star, P[3], P[2], P[1], P[0]);
  and and_5 (and_5_out, G[2], P[3]);
  xor C4 (Cout[3], G[3], and_5_out, and_6_out, and_7_out, and_8_out);
  and and_6 (and_6_out, G[1], P[3], P[2]);
  and and_7 (and_7_out, G[0], P[3], P[2], P[1]);
  and and_8 (and_8_out, P[3], P[2], P[1], P[0], C0);
  xor C3 (Cout[2], G[2], and_9_out, and_10_out, and_11_out);
  and and_9 (and_9_out, G[1], P[2]);
  and and_10 (and_10_out, G[0], P[2], P[1]);
  and and_11 (and_11_out, P[2], P[1], P[0], C0);
  xor C2 (Cout[1], G[1], and_12_out, and_13_out);
  and and_12 (and_12_out, G[0], P[1]);
  and and_13 (and_13_out, P[1], P[0], C0);
  xor C1 (Cout[0], G[0], and_14_out);
  and and_14 (and_14_out, P[0], C0);
endmodule

module _4_bits_add (
  input  [3:0] X,
  input  [3:0] Y,
  input  C0,
  output Cout,
  output [3:0] out,
  output G_star,
  output P_star
);

  wire [2:0] cla_1_cout;
  wire [3:0] and_1_out, xor_3_out;

  xor xor_1 (out[3], cla_1_cout[2], X[3], Y[3]);
  CLA cla_1 (.G(and_1_out), .P(xor_3_out), .C0(C0), .Cout({Cout, cla_1_cout}), .P_star(P_star), .G_star(G_star));
  xor xor_2 (out[2], cla_1_cout[1], X[2], Y[2]);
  assign and_1_out = X & Y;  // AND_Gate and_1, 4 bits wide
  assign xor_3_out = X ^ Y;  // XOR_Gate xor_3, 4 bits wide
  xor xor_4 (out[1], cla_1_cout[0], X[1], Y[1]);
  xor xor_5 (out[0], X[0], Y[0], C0);
endmodule

module _32_bits_add (
  input  in_1,
  input  in_2,
  input  [31:0] X,
  input  [31:0] Y,
  output [31:0] out
);

  wire [1:0] cla_3_g_star, cla_3_p_star;
  wire [3:0] cla_1_cout, cla_2_cout, cla_3_cout, n4_bits_add_4_g_star, n4_bits_add_4_p_star,
       n4_bits_add_8_g_star, n4_bits_add_8_p_star;

  _4_bits_add u_4_bits_add_1 (
    .X(X[31:28]), .Y(Y[31:28]), .out(out[31:28]), .C0(cla_1_cout[2]), .P_star(n4_bits_add_4_p_star[3]),
    .G_star(n4_bits_add_4_g_star[3]));  // open: Cout
  _4_bits_add u_4_bits_add_2 (
    .X(X[27:24]), .Y(Y[27:24]), .out(out[27:24]), .C0(cla_1_cout[1]), .P_star(n4_bits_add_4_p_star[2]),
    .G_star(n4_bits_add_4_g_star[2]));  // open: Cout
  _4_bits_add u_4_bits_add_3 (
    .X(X[23:20]), .Y(Y[23:20]), .out(out[23:20]), .C0(cla_1_cout[0]), .P_star(n4_bits_add_4_p_star[1]),
    .G_star(n4_bits_add_4_g_star[1]));  // open: Cout
  CLA cla_1 (
    .G(n4_bits_add_4_p_star), .P(n4_bits_add_4_g_star), .C0(cla_2_cout[0]), .Cout(cla_1_cout),
    .P_star(cla_3_p_star[1]), .G_star(cla_3_g_star[1]));
  _4_bits_add u_4_bits_add_4 (
    .X(X[19:16]), .Y(Y[19:16]), .out(out[19:16]), .C0(cla_2_cout[0]), .P_star(n4_bits_add_4_p_star[0]),
    .G_star(n4_bits_add_4_g_star[0]));  // open: Cout
  _4_bits_add u_4_bits_add_5 (
    .X(X[15:12]), .Y(Y[15:12]), .out(out[15:12]), .C0(cla_3_cout[2]), .P_star(n4_bits_add_8_p_star[3]),
    .G_star(n4_bits_add_8_g_star[3]));  // open: Cout
  CLA cla_2 (
    .G({{2{in_1}}, cla_3_p_star}), .P({{2{in_1}}, cla_3_g_star}), .C0(in_2), .Cout(cla_2_cout));  // open: P_star, G_star
  _4_bits_add u_4_bits_add_6 (
    .X(X[11:8]), .Y(Y[11:8]), .out(out[11:8]), .C0(cla_3_cout[1]), .P_star(n4_bits_add_8_p_star[2]),
    .G_star(n4_bits_add_8_g_star[2]));  // open: Cout
  _4_bits_add u_4_bits_add_7 (
    .X(X[7:4]), .Y(Y[7:4]), .out(out[7:4]), .C0(cla_3_cout[0]), .P_star(n4_bits_add_8_p_star[1]),
    .G_star(n4_bits_add_8_g_star[1]));  // open: Cout
  CLA cla_3 (
    .G(n4_bits_add_8_p_star), .P(n4_bits_add_8_g_star), .C0(in_2), .Cout(cla_3_cout),
    .P_star(cla_3_p_star[0]), .G_star(cla_3_g_star[0]));
  _4_bits_add u_4_bits_add_8 (
    .X(X[3:0]), .Y(Y[3:0]), .out(out[3:0]), .C0(in_2), .P_star(n4_bits_add_8_p_star[0]),
    .G_star(n4_bits_add_8_g_star[0]));  // open: Cout
endmodule
